// Logisim project LAB1.circ as structural Verilog
module _2_1 (
  input  A,
  input  B,
  input  S,
  output Output
);

  wire and_1_out, and_2_out, not_1_out;

  not not_1 (not_1_out, S);
  and and_1 (and_1_out, A, not_1_out);
  and and_2 (and_2_out, B, S);
  or or_1 (Output, and_1_out, and_2_out);
endmodule

module _4_1 (
  input  in_1,
  input  in_2,
  input  in_3,
  input  in_4,
  input  in_5,
  input  in_6,
  output out_7
);

  wire n2_1_1_output, n2_1_2_output;

  _2_1 u_2_1_1 (.A(in_1), .B(in_2), .S(in_5), .Output(n2_1_1_output));
  _2_1 u_2_1_2 (.A(in_3), .B(in_4), .S(in_5), .Output(n2_1_2_output));
  _2_1 u_2_1_3 (.A(n2_1_1_output), .B(n2_1_2_output), .S(in_6), .Output(out_7));
endmodule

module _8_1 (
  input  in_1,
  input  in_2,
  input  in_3,
  input  in_4,
  input  in_5,
  input  in_6,
  input  in_7,
  input  in_8,
  input  in_9,
  input  in_10,
  input  in_11,
  output out_12
);

  wire n4_1_1_out_7, n4_1_2_out_7;

  _4_1 u_4_1_1 (.in_1(in_1), .in_2(in_2), .in_3(in_3), .in_4(in_4), .in_5(in_9), .in_6(in_10), .out_7(n4_1_1_out_7));
  _4_1 u_4_1_2 (.in_1(in_5), .in_2(in_6), .in_3(in_7), .in_4(in_8), .in_5(in_9), .in_6(in_10), .out_7(n4_1_2_out_7));
  _2_1 u_2_1_1 (.A(n4_1_1_out_7), .B(n4_1_2_out_7), .S(in_11), .Output(out_12));
endmodule
